# Fritzing sketch TFT (saved by Fritzing 0.9.4)
breadboards: 1
perfboards: 1

parts:
  Part1 = Arduino Mega 2560 (Rev3)
  Part2 = 3.5in TFT 480x320 Touch + MicroSD
  Part3 = Arduino Mega 2560 (Rev3)  # not connected
  Part4 = 3.5in TFT 480x320 Touch + MicroSD
  S1 = Toggle Switch [package=THT]
  R2 = Rotary Potentiometer (Large) [maximum_resistance=100kΩ package=THT]
  R3 = Photocell (LDR) [package=THT]
  R4 = Resistor [tolerance=±5% resistance=220 package=THT]
  R5 = Rotary Potentiometer (Large) [maximum_resistance=100kΩ package=THT]
  R6 = Photocell (LDR) [package=THT]  # not connected
  R7 = Resistor [tolerance=±5% resistance=220 package=THT]

nets:
  N1: Part1.A0, R2.wiper
  N2: Part1.A2, Part2.LCD_Y+
  N3: Part1.A3, Part2.LCD_X-
  N4: Part1.A4, R3.pin_1, R4.Pin_0
  N5: Part1.D11_PWM, Part2.LCD_LITE
  N6: Part1.D10_PWM, Part2.LCD_RS_5V
  N7: Part1.D9_PWM, Part2.LCD_CS_5V
  N8: Part1.D8_PWM, Part2.LCD_X+
  5V: Part1.5V, Part2.+5V, R2.leg2, R3.pin_0
  GND: Part1.GND, Part2.GND, R4.Pin_1
  N9: Part1.D5_PWM, Part2.Card_CS
  N10: Part1.D7_PWM, Part2.LCD_Y-
  N11: Part1.D50, Part2.MISO
  N12: Part1.D51, Part2.MOSI
  N13: Part1.D52, Part2.LCD_WR_5V
  N14: Part4.3-5V, Part4.+5V, S1.L1
  N15: Part4.CS, Part4.LCD_CS_5V
  N16: Part4.C/D, Part4.LCD_RS_5V
  N17: Part4.WR/SPI_CLK, Part4.LCD_WR_5V
  N18: Part4.RST, Part4.LCD_RST_5V
  N19: Part4.Backlite/Lite, Part4.LCD_LITE
  N20: R5.leg1, R7.Pin_1

custom parts:
  3.5in TFT 480x320 Touch + MicroSD: This TFT display is big (3.5" diagonal), bright (6 white-LED backlight) and colorful! 480x320 pixels with individual RGB pixel control. This display also has a resistive touchscreen attached to it already, so you can detect finger presses anywhere on the screen. There is a controller built into the display with RAM buffering, so that almost no work is done by the microcontroller. The display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
